// Logisim project lab2.circ as structural Verilog
module SR_Latch (
  input  Reset,
  input  Set,
  output Q,
  output Not_Q
);

  nor nor_1 (Q, Reset, Not_Q);
  nor nor_2 (Not_Q, Q, Set);
endmodule

module D_Latch (
  input  CLK,
  input  Data,
  output Q,
  output Not_Q
);

  wire and_1_out, and_2_out, not_1_out;

  not not_1 (not_1_out, Data);
  and and_1 (and_1_out, CLK, not_1_out);
  and and_2 (and_2_out, CLK, Data);
  SR_Latch sr_latch_1 (.Reset(and_1_out), .Set(and_2_out), .Q(Q), .Not_Q(Not_Q));
endmodule

module D_FlipFlop (
  input  CLK,
  input  Data,
  output Q,
  output Not_Q
);

  wire first_q, not_1_out;

  not not_1 (not_1_out, CLK);
  D_Latch first (.CLK(not_1_out), .Data(Data), .Q(first_q));  // open: Not_Q
  D_Latch d_latch_1 (.CLK(CLK), .Data(first_q), .Q(Q), .Not_Q(Not_Q));
endmodule

module D_FlipFlop_Reset (
  input  CLK,
  input  Data,
  input  Reset,
  output Q,
  output Not_Q
);

  wire and_1_out, not_1_out;

  not not_1 (not_1_out, Reset);
  and and_1 (and_1_out, Data, not_1_out);
  D_FlipFlop d_flipflop_1 (.CLK(CLK), .Data(and_1_out), .Q(Q), .Not_Q(Not_Q));
endmodule

module Reg_4bit (
  input  [3:0] in_1,
  input  CLK,
  output [3:0] out_3
);

  D_FlipFlop d_flipflop_1 (.CLK(CLK), .Data(in_1[0]), .Q(out_3[0]));  // open: Not_Q
  D_FlipFlop d_flipflop_2 (.CLK(CLK), .Data(in_1[1]), .Q(out_3[1]));  // open: Not_Q
  D_FlipFlop d_flipflop_3 (.CLK(CLK), .Data(in_1[2]), .Q(out_3[2]));  // open: Not_Q
  D_FlipFlop d_flipflop_4 (.CLK(CLK), .Data(in_1[3]), .Q(out_3[3]));  // open: Not_Q
endmodule

module CountDown_2bit (
);

  wire comparator_1_eq, undriven;
  wire [3:0] adder_1_out, multiplexer_1_out, reg_4bit_1_out_3;

  Adder #(.width(4)) adder_1 (.a(reg_4bit_1_out_3), .b(4'b0001), .out(adder_1_out));  // open: cin, cout
  Comparator #(.width(4)) comparator_1 (.a(reg_4bit_1_out_3), .b(4'b1001), .eq(comparator_1_eq));  // open: gt, lt
  Multiplexer #(.width(4)) multiplexer_1 (
    .in0(adder_1_out), .in1(4'b0000), .out(multiplexer_1_out), .sel(comparator_1_eq));
  Reg_4bit reg_4bit_1 (.in_1(multiplexer_1_out), .CLK(undriven), .out_3(reg_4bit_1_out_3));
  Clock clock_1 ();  // open: out
endmodule
