// Logisim project lab3.circ as structural Verilog: 6 circuits, main circuit main
module main (
  input  Reset
);

  wire and_1_out, and_2_out, and_3_out, and_4_out, and_5_out, and_6_out, clock_1_out, d_ff_1_q, d_ff_2_q,
       not_1_out, not_2_out, not_3_out, not_4_out, not_5_out, or_1_out, or_2_out, P_out;

  Button P (.out(P_out));
  not not_1 (not_1_out, P_out);
  not not_2 (not_2_out, d_ff_1_q);
  not not_3 (not_3_out, d_ff_2_q);
  and and_1 (and_1_out, d_ff_1_q, not_1_out);
  and and_2 (and_2_out, d_ff_2_q, P_out);
  and and_3 (and_3_out, not_1_out, d_ff_2_q);
  and and_4 (and_4_out, not_2_out, not_3_out);
  or or_1 (or_1_out, and_1_out, and_2_out);
  or or_2 (or_2_out, and_3_out, and_4_out);
  Clock clock_1 (.out(clock_1_out));
  D_Flip_Flop d_ff_1 (.D(or_1_out), .clk(clock_1_out), .Q(d_ff_1_q), .reset(Reset));  // open: Qn, preset
  D_Flip_Flop d_ff_2 (.D(or_2_out), .clk(clock_1_out), .Q(d_ff_2_q), .reset(Reset));  // open: Qn, preset
  not not_4 (not_4_out, d_ff_1_q);
  not not_5 (not_5_out, d_ff_2_q);
  and and_5 (and_5_out, d_ff_1_q, not_5_out);
  and and_6 (and_6_out, not_4_out, d_ff_2_q);
  LED led_1 (.in(and_5_out));
  LED led_2 (.in(and_6_out));
endmodule

module next_state (
  input  S1,
  input  S0,
  input  Ta,
  input  Tb,
  output S1_next,
  output S0_next
);

  wire and_1_out, and_2_out, and_3_out, and_4_out, not_1_out, not_2_out, not_3_out, not_4_out;

  not not_1 (not_1_out, S1);
  not not_2 (not_2_out, S0);
  not not_3 (not_3_out, Ta);
  not not_4 (not_4_out, Tb);
  and and_1 (and_1_out, not_1_out, S0);
  and and_2 (and_2_out, S1, not_2_out);
  and and_3 (and_3_out, not_1_out, not_2_out, not_3_out);
  and and_4 (and_4_out, S1, not_2_out, not_4_out);
  or or_1 (S1_next, and_1_out, and_2_out);
  or or_2 (S0_next, and_3_out, and_4_out);
endmodule

module Traffic_light_controller (
  input  Reset
);

  wire clock_1_out, d_ff_1_q, d_ff_2_q, next_state_1_s0_next, next_state_1_s1_next,
       output_logic_1_light_a_grn, output_logic_1_light_a_red, output_logic_1_light_a_ylw,
       output_logic_1_light_b_grn, output_logic_1_light_b_red, output_logic_1_light_b_ylw, Ta_out, Tb_out;

  Button Ta (.out(Ta_out));
  Button Tb (.out(Tb_out));
  Clock clock_1 (.out(clock_1_out));
  next_state next_state_1 (
    .S1(d_ff_1_q), .S0(d_ff_2_q), .Ta(Ta_out), .Tb(Tb_out), .S1_next(next_state_1_s1_next),
    .S0_next(next_state_1_s0_next));
  D_Flip_Flop d_ff_1 (.D(next_state_1_s1_next), .clk(clock_1_out), .Q(d_ff_1_q), .reset(Reset));  // open: Qn, preset
  D_Flip_Flop d_ff_2 (.D(next_state_1_s0_next), .clk(clock_1_out), .Q(d_ff_2_q), .reset(Reset));  // open: Qn, preset
  output_logic output_logic_1 (
    .S1(d_ff_1_q), .S0(d_ff_2_q), .Light_A_GRN(output_logic_1_light_a_grn),
    .Light_A_YLW(output_logic_1_light_a_ylw), .Light_A_RED(output_logic_1_light_a_red),
    .Light_B_GRN(output_logic_1_light_b_grn), .Light_B_YLW(output_logic_1_light_b_ylw),
    .Light_B_RED(output_logic_1_light_b_red));
  LED led_1 (.in(output_logic_1_light_a_grn));
  LED led_2 (.in(output_logic_1_light_a_ylw));
  LED led_3 (.in(output_logic_1_light_a_red));
  LED led_4 (.in(output_logic_1_light_b_grn));
  LED led_5 (.in(output_logic_1_light_b_ylw));
  LED led_6 (.in(output_logic_1_light_b_red));
endmodule

module output_logic (
  input  S1,
  input  S0,
  output Light_A_GRN,
  output Light_A_YLW,
  output Light_A_RED,
  output Light_B_GRN,
  output Light_B_YLW,
  output Light_B_RED
);

  wire not_2_out;

  not not_1 (Light_B_RED, S1);
  not not_2 (not_2_out, S0);
  and and_1 (Light_A_GRN, Light_B_RED, not_2_out);
  and and_2 (Light_A_YLW, Light_B_RED, S0);
  and and_3 (Light_B_GRN, S1, not_2_out);
  and and_4 (Light_B_YLW, S1, S0);

  assign Light_A_RED = S1;
endmodule

module JMU (
  input  Rest
);

  wire and_1_out, clock_1_out, comparator_1_eq, comparator_2_eq, comparator_3_eq, d_ff_1_q, d_ff_2_q,
       next_state1_1_s0_next, next_state1_1_s1_next, not_1_out, or_1_out;
  wire [6:0] keyboard_1_data;

  Keyboard keyboard_1 (.clk(clock_1_out), .data(keyboard_1_data));  // open: re, clr, avail
  Comparator #(.width(7)) comparator_1 (.a(keyboard_1_data), .b(7'b1001010), .eq(comparator_1_eq));  // open: gt, lt
  Comparator #(.width(7)) comparator_2 (.a(keyboard_1_data), .b(7'b1001101), .eq(comparator_2_eq));  // open: gt, lt
  Comparator #(.width(7)) comparator_3 (.a(keyboard_1_data), .b(7'b1010101), .eq(comparator_3_eq));  // open: gt, lt
  or or_1 (or_1_out, comparator_1_eq, comparator_3_eq, comparator_2_eq);
  Clock clock_1 (.out(clock_1_out));
  next_state1 next_state1_1 (
    .S1(d_ff_1_q), .S0(d_ff_2_q), .C(or_1_out), .S1_next(next_state1_1_s1_next),
    .S0_next(next_state1_1_s0_next));
  D_Flip_Flop d_ff_1 (.D(next_state1_1_s1_next), .clk(clock_1_out), .Q(d_ff_1_q), .reset(Rest));  // open: Qn, preset
  D_Flip_Flop d_ff_2 (.D(next_state1_1_s0_next), .clk(clock_1_out), .Q(d_ff_2_q), .reset(Rest));  // open: Qn, preset
  not not_1 (not_1_out, d_ff_1_q);
  and and_1 (and_1_out, d_ff_2_q, not_1_out, comparator_3_eq);
  TTY tty_1 (.data(7'b1010110), .clk(and_1_out));  // open: we, clr
endmodule

module next_state1 (
  input  S1,
  input  S0,
  input  C,
  output S1_next,
  output S0_next
);

  wire and_2_out, and_3_out, not_1_out, not_2_out;

  not not_1 (not_1_out, S0);
  not not_2 (not_2_out, C);
  and and_1 (S1_next, S0, C);
  and and_2 (and_2_out, not_1_out, C);
  and and_3 (and_3_out, S0, not_2_out);
  or or_1 (S0_next, and_2_out, and_3_out);
endmodule
